# Fritzing sketch prototipo (saved by Fritzing 0.9.3b)
circuit board: 10cm x 10cm
breadboards: 3

parts:
  Componente1 = Adafruit ADS1115 16Bit I2C ADC [part_number="Adafruit #1085"]
  M1 = ESP32-S3-DevKitC-1-N8R8-v1 [part_number=ESP32-S3-DevKitC-1-N8R8-v1]
  Componente2 = ACS712 Current Sensor 5A 20A 30A
  LCD1 = TFT 1.8 inch 160x128 w SD
  KY-1 = Keyes Relay [package=THT]
  M2 = HLK-5M05
  Q1 = TRANSISTOR_NPN [package=to-92-ammo]
  J1 = Buzzer
  R1 = TRIMPOT [package=trimpot_pth_s3_lock]
  R2 = TRIMPOT [package=trimpot_pth_s3_lock]
  R3 = Resistor [tolerance=±5% resistance=630k package="2010 [SMD]"]
  R4 = Resistor [tolerance=±5% resistance=630k package="2010 [SMD]"]

nets:
  N1: Componente1.AIN3, R2.WIPER, R4.Pin_1
  N2: Componente1.AIN2, R1.WIPER, R3.Pin_1
  N3: Componente1.AIN1, Componente2.2, Componente2.OUT
  N4: Componente1.SDA, M1.pin_12
  N5: Componente1.SCL, M1.pin_15
  GND: Componente1.GND, M1.pin_22, Componente2.GND, LCD1.pin2, KY-1.power, KY-1.ground, M2.-Vo, Q1.C, R1.CW, R2.CCW
  VDD: Componente1.VDD, Componente2.VCC, M2.+Vo, J1.pin2
  N6: M1.pin_1, M1.pin_2, LCD1.pin_1
  N7: M1.pin_5, LCD1.pin4
  N8: M1.pin_6, LCD1.pin_5
  N9: M1.pin_9, LCD1.pin_8
  N10: M1.pin_16, LCD1.pin3
  N11: M1.pin_17, LCD1.pin_6
  N12: M1.pin_18, LCD1.pin_7
  N13: M1.pin_19, Q1.B
  N14: M1.pin_20, M1.pin_21, KY-1.signal
  N15: Componente2.1, KY-1.NC, R3.Pin_0
  N16: KY-1.C, M2.pin_1, M2.pin_2, R4.Pin_0
  N17: Q1.E, J1.pin1

custom parts:
  Adafruit ADS1115 16Bit I2C ADC: For microcontrollers without an analog-to-digital converter or when you want a higher-precision ADC, the ADS1115 provides 16-bit precision at 860 samples/second over I2C. The chip can be configured as 4 single-ended input channels, or two differential channels. As a nice bonus, it even includes a programmable gain amplifier, up to x16, to help boost up smaller single/differential signals to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
  ESP32-S3-DevKitC-1-N8R8-v1: ESP32-S3-DevKitC-1-N8R8-v1 This module is 44pins long (2x22) and 11 pins width.
  ACS712 Current Sensor 5A 20A 30A: Remix by Michael Kubina http://www.kubina.info Original by: https://forum.fritzing.org/t/current-sensor-5a-acs712/7694 https://forum.fritzing.org/u/ArtHome ArtHome12@gmail.com
  TFT 1.8 inch 160x128 w SD: This is a generic 1.8 tft spi lcd display available on ebay and others. The 1.8" display has 128x160 color pixels.
  Keyes Relay: The Keyes 5V relay module is suitable for SCM development, home appliance control. It uses a 5V~12V TIL control signal which can control DC / AC signal.
  HLK-5M05: AC-DC 220V to 5V Step-Down Power Supply Module
  Buzzer: Fixed frequency buzzer
